// Logisim project Final-8_bit_left.circ as structural Verilog: 3 circuits, main circuit main
module main (
  input  Left_in,
  input  In,
  output out_3,
  output out_4,
  output out_5,
  output out_6,
  output out_7,
  output out_8,
  output out_9,
  output out_10
);

  wire CLK_out, multiplexer_1_out, multiplexer_2_out, multiplexer_3_out, multiplexer_4_out,
       multiplexer_5_out, multiplexer_6_out, multiplexer_7_out, multiplexer_8_out;

  Clock CLK (.out(CLK_out));
  Multiplexer multiplexer_1 (.in1(In), .out(multiplexer_1_out), .sel(Left_in));  // open: in0, en
  D_Flip_Flop d_ff_1 (.clk(CLK_out), .D(multiplexer_1_out), .Q(out_3));  // open: Qn, preset, en, reset
  Multiplexer multiplexer_2 (.in1(out_3), .out(multiplexer_2_out), .sel(Left_in));  // open: in0, en
  D_Flip_Flop d_ff_2 (.clk(CLK_out), .D(multiplexer_2_out), .Q(out_4));  // open: Qn, preset, en, reset
  Multiplexer multiplexer_3 (.in1(out_4), .out(multiplexer_3_out), .sel(Left_in));  // open: in0, en
  D_Flip_Flop d_ff_3 (.clk(CLK_out), .D(multiplexer_3_out), .Q(out_5));  // open: Qn, preset, en, reset
  Multiplexer multiplexer_4 (.in1(out_5), .out(multiplexer_4_out), .sel(Left_in));  // open: in0, en
  D_Flip_Flop d_ff_4 (.clk(CLK_out), .D(multiplexer_4_out), .Q(out_7));  // open: Qn, preset, en, reset
  Multiplexer multiplexer_5 (.in1(out_7), .out(multiplexer_5_out), .sel(Left_in));  // open: in0, en
  D_Flip_Flop d_ff_5 (.clk(CLK_out), .D(multiplexer_5_out), .Q(out_9));  // open: Qn, preset, en, reset
  Multiplexer multiplexer_6 (.in1(out_9), .out(multiplexer_6_out), .sel(Left_in));  // open: in0, en
  D_Flip_Flop d_ff_6 (.clk(CLK_out), .D(multiplexer_6_out), .Q(out_6));  // open: Qn, preset, en, reset
  Multiplexer multiplexer_7 (.in1(out_6), .out(multiplexer_7_out), .sel(Left_in));  // open: in0, en
  D_Flip_Flop d_ff_7 (.clk(CLK_out), .D(multiplexer_7_out), .Q(out_10));  // open: Qn, preset, en, reset
  Multiplexer multiplexer_8 (.in0(In), .in1(out_10), .out(multiplexer_8_out), .sel(Left_in));  // open: en
  D_Flip_Flop d_ff_8 (.clk(CLK_out), .D(multiplexer_8_out), .Q(out_8));  // open: Qn, preset, en, reset
endmodule

module right (
  input  Left_in,
  input  In,
  output out_3,
  output out_4,
  output out_5,
  output out_6,
  output out_7,
  output out_8,
  output out_9,
  output out_10
);

  wire clock_1_out, multiplexer_1_out, multiplexer_2_out, multiplexer_3_out, multiplexer_4_out,
       multiplexer_5_out, multiplexer_6_out, multiplexer_7_out, multiplexer_8_out;

  Clock clock_1 (.out(clock_1_out));
  D_Flip_Flop d_ff_1 (.clk(clock_1_out), .D(multiplexer_1_out), .Q(out_4));  // open: Qn, preset, en, reset
  Multiplexer multiplexer_1 (.in0(out_3), .out(multiplexer_1_out), .sel(Left_in));  // open: in1, en
  D_Flip_Flop d_ff_2 (.clk(clock_1_out), .D(multiplexer_2_out), .Q(out_3));  // open: Qn, preset, en, reset
  Multiplexer multiplexer_2 (.in0(out_8), .out(multiplexer_2_out), .sel(Left_in));  // open: in1, en
  D_Flip_Flop d_ff_3 (.clk(clock_1_out), .D(multiplexer_3_out), .Q(out_8));  // open: Qn, preset, en, reset
  Multiplexer multiplexer_3 (.in0(out_5), .out(multiplexer_3_out), .sel(Left_in));  // open: in1, en
  Multiplexer multiplexer_4 (.in0(out_6), .out(multiplexer_4_out), .sel(Left_in));  // open: in1, en
  D_Flip_Flop d_ff_4 (.clk(clock_1_out), .D(multiplexer_4_out), .Q(out_5));  // open: Qn, preset, en, reset
  D_Flip_Flop d_ff_5 (.clk(clock_1_out), .D(multiplexer_5_out), .Q(out_6));  // open: Qn, preset, en, reset
  Multiplexer multiplexer_5 (.in0(out_7), .out(multiplexer_5_out), .sel(Left_in));  // open: in1, en
  D_Flip_Flop d_ff_6 (.clk(clock_1_out), .D(multiplexer_6_out), .Q(out_7));  // open: Qn, preset, en, reset
  Multiplexer multiplexer_6 (.in0(out_9), .out(multiplexer_6_out), .sel(Left_in));  // open: in1, en
  Multiplexer multiplexer_7 (.in0(out_10), .out(multiplexer_7_out), .sel(Left_in));  // open: in1, en
  D_Flip_Flop d_ff_7 (.clk(clock_1_out), .D(multiplexer_7_out), .Q(out_9));  // open: Qn, preset, en, reset
  D_Flip_Flop d_ff_8 (.clk(clock_1_out), .D(multiplexer_8_out), .Q(out_10));  // open: Qn, preset, en, reset
  Multiplexer multiplexer_8 (.in0(In), .out(multiplexer_8_out), .sel(Left_in));  // open: in1, en
endmodule

module Combined (
  input  LOAD,
  input  in7,
  input  in6,
  input  in5,
  input  in4,
  input  in3,
  input  in2,
  input  in1,
  input  in0,
  input  left_in,
  input  in3_2,
  input  in4_2,
  input  in6_2,
  input  in0_2,
  input  in1_2,
  input  in2_2,
  input  in5_2,
  input  in7_2,
  input  LOAD_2,
  output out0,
  output out1,
  output out2,
  output out3,
  output out4,
  output out5,
  output out6,
  output out7
);

  wire CLK_2_out, CLK_out, d_ff_1_q, d_ff_2_q, d_ff_3_q, d_ff_4_q, d_ff_5_q, d_ff_6_q, d_ff_7_q, d_ff_8_q,
       d_ff_9_q, d_ff_10_q, d_ff_11_q, d_ff_12_q, d_ff_13_q, d_ff_14_q, d_ff_15_q, d_ff_16_q,
       multiplexer_1_out, multiplexer_2_out, multiplexer_3_out, multiplexer_6_out, multiplexer_7_out,
       multiplexer_9_out, multiplexer_10_out, multiplexer_12_out, multiplexer_14_out, multiplexer_16_out,
       multiplexer_17_out, multiplexer_18_out, multiplexer_20_out, multiplexer_21_out, multiplexer_23_out,
       multiplexer_24_out;

  Multiplexer multiplexer_1 (.in0(d_ff_3_q), .in1(in7), .out(multiplexer_1_out), .sel(LOAD));  // open: en
  Clock CLK (.out(CLK_out));
  Clock CLK_2 (.out(CLK_2_out));
  D_Flip_Flop d_ff_1 (.clk(CLK_out), .D(multiplexer_1_out), .Q(d_ff_1_q));  // open: Qn, preset, en, reset
  D_Flip_Flop d_ff_2 (.clk(CLK_2_out), .D(multiplexer_2_out), .Q(d_ff_2_q));  // open: Qn, preset, en, reset
  Multiplexer multiplexer_2 (.in0(d_ff_16_q), .in1(in0_2), .out(multiplexer_2_out), .sel(LOAD_2));  // open: en
  Multiplexer multiplexer_3 (.in0(d_ff_5_q), .in1(in6), .out(multiplexer_3_out), .sel(LOAD));  // open: en
  Multiplexer multiplexer_4 (.in0(d_ff_1_q), .in1(d_ff_2_q), .out(out0), .sel(left_in));  // open: en
  Multiplexer multiplexer_5 (.in0(d_ff_3_q), .in1(d_ff_4_q), .out(out1), .sel(left_in));  // open: en
  Multiplexer multiplexer_6 (.in0(d_ff_2_q), .in1(in1_2), .out(multiplexer_6_out), .sel(LOAD_2));  // open: en
  D_Flip_Flop d_ff_3 (.clk(CLK_out), .D(multiplexer_3_out), .Q(d_ff_3_q));  // open: Qn, preset, en, reset
  D_Flip_Flop d_ff_4 (.clk(CLK_2_out), .D(multiplexer_6_out), .Q(d_ff_4_q));  // open: Qn, preset, en, reset
  Multiplexer multiplexer_7 (.in0(d_ff_7_q), .in1(in5), .out(multiplexer_7_out), .sel(LOAD));  // open: en
  Multiplexer multiplexer_8 (.in0(d_ff_5_q), .in1(d_ff_6_q), .out(out2), .sel(left_in));  // open: en
  D_Flip_Flop d_ff_5 (.clk(CLK_out), .D(multiplexer_7_out), .Q(d_ff_5_q));  // open: Qn, preset, en, reset
  D_Flip_Flop d_ff_6 (.clk(CLK_2_out), .D(multiplexer_9_out), .Q(d_ff_6_q));  // open: Qn, preset, en, reset
  Multiplexer multiplexer_9 (.in0(d_ff_4_q), .in1(in2_2), .out(multiplexer_9_out), .sel(LOAD_2));  // open: en
  Multiplexer multiplexer_10 (.in0(d_ff_9_q), .in1(in4), .out(multiplexer_10_out), .sel(LOAD));  // open: en
  Multiplexer multiplexer_11 (.in0(d_ff_7_q), .in1(d_ff_8_q), .out(out3), .sel(left_in));  // open: en
  D_Flip_Flop d_ff_7 (.clk(CLK_out), .D(multiplexer_10_out), .Q(d_ff_7_q));  // open: Qn, preset, en, reset
  D_Flip_Flop d_ff_8 (.clk(CLK_2_out), .D(multiplexer_12_out), .Q(d_ff_8_q));  // open: Qn, preset, en, reset
  Multiplexer multiplexer_12 (.in0(d_ff_6_q), .in1(in3_2), .out(multiplexer_12_out), .sel(LOAD_2));  // open: en
  Multiplexer multiplexer_13 (.in0(d_ff_9_q), .in1(d_ff_10_q), .out(out4), .sel(left_in));  // open: en
  Multiplexer multiplexer_14 (.in0(d_ff_11_q), .in1(in3), .out(multiplexer_14_out), .sel(LOAD));  // open: en
  D_Flip_Flop d_ff_9 (.clk(CLK_out), .D(multiplexer_14_out), .Q(d_ff_9_q));  // open: Qn, preset, en, reset
  Multiplexer multiplexer_15 (.in0(d_ff_11_q), .in1(d_ff_12_q), .out(out5), .sel(left_in));  // open: en
  D_Flip_Flop d_ff_10 (.clk(CLK_2_out), .D(multiplexer_16_out), .Q(d_ff_10_q));  // open: Qn, preset, en, reset
  Multiplexer multiplexer_16 (.in0(d_ff_8_q), .in1(in4_2), .out(multiplexer_16_out), .sel(LOAD_2));  // open: en
  Multiplexer multiplexer_17 (.in0(d_ff_13_q), .in1(in2), .out(multiplexer_17_out), .sel(LOAD));  // open: en
  Multiplexer multiplexer_18 (.in0(d_ff_15_q), .in1(in1), .out(multiplexer_18_out), .sel(LOAD));  // open: en
  D_Flip_Flop d_ff_11 (.clk(CLK_out), .D(multiplexer_17_out), .Q(d_ff_11_q));  // open: Qn, preset, en, reset
  Multiplexer multiplexer_19 (.in0(d_ff_13_q), .in1(d_ff_14_q), .out(out6), .sel(left_in));  // open: en
  D_Flip_Flop d_ff_12 (.clk(CLK_2_out), .D(multiplexer_20_out), .Q(d_ff_12_q));  // open: Qn, preset, en, reset
  Multiplexer multiplexer_20 (.in0(d_ff_10_q), .in1(in5_2), .out(multiplexer_20_out), .sel(LOAD_2));  // open: en
  Multiplexer multiplexer_21 (.in0(d_ff_1_q), .in1(in0), .out(multiplexer_21_out), .sel(LOAD));  // open: en
  D_Flip_Flop d_ff_13 (.clk(CLK_out), .D(multiplexer_18_out), .Q(d_ff_13_q));  // open: Qn, preset, en, reset
  Multiplexer multiplexer_22 (.in0(d_ff_15_q), .in1(d_ff_16_q), .out(out7), .sel(left_in));  // open: en
  D_Flip_Flop d_ff_14 (.clk(CLK_2_out), .D(multiplexer_23_out), .Q(d_ff_14_q));  // open: Qn, preset, en, reset
  Multiplexer multiplexer_23 (.in0(d_ff_12_q), .in1(in6_2), .out(multiplexer_23_out), .sel(LOAD_2));  // open: en
  D_Flip_Flop d_ff_15 (.clk(CLK_out), .D(multiplexer_21_out), .Q(d_ff_15_q));  // open: Qn, preset, en, reset
  D_Flip_Flop d_ff_16 (.clk(CLK_2_out), .D(multiplexer_24_out), .Q(d_ff_16_q));  // open: Qn, preset, en, reset
  Multiplexer multiplexer_24 (.in0(d_ff_14_q), .in1(in7_2), .out(multiplexer_24_out), .sel(LOAD_2));  // open: en

  // Notes on the sheet:
  //   Right Shift Area
  //   Left Or Right Shift Mux
  //   Left Shift Area
endmodule
