// Logisim project shifter.circ as structural Verilog: 1 circuit, main circuit main
module main (
  input  in_1,
  input  in_2,
  input  LOAD,
  input  _7_0__D,
  input  in_5,
  input  in_6,
  input  in_7,
  input  in_8,
  input  in_9,
  input  in_10,
  input  in_11,
  input  in_12,
  output out_13,
  output out_14,
  output out_15,
  output out_16,
  output out_17,
  output out_18,
  output out_19,
  output out_20
);

  wire clock_1_out, d_ff_2_q, d_ff_3_q, d_ff_4_q, d_ff_5_q, d_ff_6_q, d_ff_7_q, d_ff_8_q, d_ff_9_q,
       d_ff_10_q, d_ff_11_q, d_ff_12_q, d_ff_13_q, d_ff_14_q, d_ff_15_q, d_ff_16_q, multiplexer_1_out,
       multiplexer_2_out, multiplexer_4_out, multiplexer_5_out, multiplexer_7_out, multiplexer_8_out,
       multiplexer_10_out, multiplexer_11_out, multiplexer_13_out, multiplexer_14_out, multiplexer_16_out,
       multiplexer_17_out, multiplexer_18_out, multiplexer_20_out, multiplexer_22_out, multiplexer_23_out;

  Clock clock_1 (.out(clock_1_out));
  D_Flip_Flop d_ff_1 (.clk(clock_1_out), .D(multiplexer_2_out));  // open: Q, Qn, preset, en, reset
  Multiplexer #(.enable("false")) multiplexer_1 (.in0(in_1), .in1(_7_0__D), .out(multiplexer_1_out), .sel(LOAD));
  Multiplexer #(.enable("false")) multiplexer_2 (.in0(d_ff_3_q), .out(multiplexer_2_out), .sel(LOAD));  // open: in1
  D_Flip_Flop d_ff_2 (.clk(clock_1_out), .D(multiplexer_1_out), .Q(d_ff_2_q));  // open: Qn, preset, en, reset
  Multiplexer #(.enable("false")) multiplexer_3 (.in0(d_ff_2_q), .out(out_13), .sel(in_2));  // open: in1
  D_Flip_Flop d_ff_3 (.clk(clock_1_out), .D(multiplexer_4_out), .Q(d_ff_3_q));  // open: Qn, preset, en, reset
  Multiplexer #(.enable("false")) multiplexer_4 (.in0(d_ff_5_q), .in1(in_11), .out(multiplexer_4_out), .sel(LOAD));
  Multiplexer #(.enable("false")) multiplexer_5 (.in0(d_ff_2_q), .in1(in_5), .out(multiplexer_5_out), .sel(LOAD));
  D_Flip_Flop d_ff_4 (.clk(clock_1_out), .D(multiplexer_5_out), .Q(d_ff_4_q));  // open: Qn, preset, en, reset
  Multiplexer #(.enable("false")) multiplexer_6 (.in0(d_ff_4_q), .out(out_14), .sel(in_2));  // open: in1
  D_Flip_Flop d_ff_5 (.clk(clock_1_out), .D(multiplexer_7_out), .Q(d_ff_5_q));  // open: Qn, preset, en, reset
  Multiplexer #(.enable("false")) multiplexer_7 (.in0(d_ff_7_q), .in1(in_10), .out(multiplexer_7_out), .sel(LOAD));
  D_Flip_Flop d_ff_6 (.clk(clock_1_out), .D(multiplexer_8_out), .Q(d_ff_6_q));  // open: Qn, preset, en, reset
  Multiplexer #(.enable("false")) multiplexer_8 (.in0(d_ff_4_q), .in1(in_6), .out(multiplexer_8_out), .sel(LOAD));
  Multiplexer #(.enable("false")) multiplexer_9 (.in0(d_ff_6_q), .out(out_15), .sel(in_2));  // open: in1
  Multiplexer #(.enable("false")) multiplexer_10 (.in0(d_ff_6_q), .in1(in_7), .out(multiplexer_10_out), .sel(LOAD));
  D_Flip_Flop d_ff_7 (.clk(clock_1_out), .D(multiplexer_11_out), .Q(d_ff_7_q));  // open: Qn, preset, en, reset
  Multiplexer #(.enable("false")) multiplexer_11 (.in0(d_ff_9_q), .in1(in_9), .out(multiplexer_11_out), .sel(LOAD));
  D_Flip_Flop d_ff_8 (.clk(clock_1_out), .D(multiplexer_10_out), .Q(d_ff_8_q));  // open: Qn, preset, en, reset
  Multiplexer #(.enable("false")) multiplexer_12 (.in0(d_ff_8_q), .out(out_16), .sel(in_2));  // open: in1
  D_Flip_Flop d_ff_9 (.clk(clock_1_out), .D(multiplexer_14_out), .Q(d_ff_9_q));  // open: Qn, preset, en, reset
  Multiplexer #(.enable("false")) multiplexer_13 (.in0(d_ff_8_q), .in1(in_8), .out(multiplexer_13_out), .sel(LOAD));
  Multiplexer #(.enable("false")) multiplexer_14 (.in0(d_ff_11_q), .in1(in_8), .out(multiplexer_14_out), .sel(LOAD));
  D_Flip_Flop d_ff_10 (.clk(clock_1_out), .D(multiplexer_13_out), .Q(d_ff_10_q));  // open: Qn, preset, en, reset
  Multiplexer #(.enable("false")) multiplexer_15 (.in0(d_ff_10_q), .out(out_17), .sel(in_2));  // open: in1
  D_Flip_Flop d_ff_11 (.clk(clock_1_out), .D(multiplexer_17_out), .Q(d_ff_11_q));  // open: Qn, preset, en, reset
  Multiplexer #(.enable("false")) multiplexer_16 (.in0(d_ff_10_q), .in1(in_9), .out(multiplexer_16_out), .sel(LOAD));
  Multiplexer #(.enable("false")) multiplexer_17 (.in0(d_ff_13_q), .in1(in_6), .out(multiplexer_17_out), .sel(LOAD));
  D_Flip_Flop d_ff_12 (.clk(clock_1_out), .D(multiplexer_16_out), .Q(d_ff_12_q));  // open: Qn, preset, en, reset
  Multiplexer #(.enable("false")) multiplexer_18 (.in0(d_ff_12_q), .in1(in_10), .out(multiplexer_18_out), .sel(LOAD));
  Multiplexer #(.enable("false")) multiplexer_19 (.in0(d_ff_12_q), .out(out_18), .sel(in_2));  // open: in1
  D_Flip_Flop d_ff_13 (.clk(clock_1_out), .D(multiplexer_20_out), .Q(d_ff_13_q));  // open: Qn, preset, en, reset
  Multiplexer #(.enable("false")) multiplexer_20 (.in0(d_ff_15_q), .in1(in_5), .out(multiplexer_20_out), .sel(LOAD));
  D_Flip_Flop d_ff_14 (.clk(clock_1_out), .D(multiplexer_18_out), .Q(d_ff_14_q));  // open: Qn, preset, en, reset
  Multiplexer #(.enable("false")) multiplexer_21 (.in0(d_ff_14_q), .out(out_19), .sel(in_2));  // open: in1
  Multiplexer #(.enable("false")) multiplexer_22 (.in0(d_ff_14_q), .in1(in_11), .out(multiplexer_22_out), .sel(LOAD));
  D_Flip_Flop d_ff_15 (.clk(clock_1_out), .D(multiplexer_23_out), .Q(d_ff_15_q));  // open: Qn, preset, en, reset
  Multiplexer #(.enable("false")) multiplexer_23 (.in0(in_12), .in1(_7_0__D), .out(multiplexer_23_out), .sel(LOAD));
  D_Flip_Flop d_ff_16 (.clk(clock_1_out), .D(multiplexer_22_out), .Q(d_ff_16_q));  // open: Qn, preset, en, reset
  Multiplexer #(.enable("false")) multiplexer_24 (.in0(d_ff_16_q), .out(out_20), .sel(in_2));  // open: in1

  // Notes on the sheet:
  //   [7:0] F
  //   LEFT
  //   CLK
endmodule
