// Logisim project simple_left.circ as structural Verilog: 3 circuits, main circuit main
module main (
  input  SI,
  input  PI,
  input  in_3,
  input  in_4,
  input  in_5,
  input  in_6,
  input  in_7,
  input  in_8,
  input  in_9,
  output out_10,
  output out_11,
  output out_12,
  output out_13,
  output out_14,
  output out_15,
  output out_16,
  output out_17
);

  wire clock_1_out;

  Clock clock_1 (.out(clock_1_out));
  D_Flip_Flop d_ff_1 (.clk(clock_1_out), .D(SI), .Q(out_10));  // open: Qn, preset, en, reset
  D_Flip_Flop d_ff_2 (.clk(clock_1_out), .D(out_10), .Q(out_11));  // open: Qn, preset, en, reset
  D_Flip_Flop d_ff_3 (.clk(clock_1_out), .D(out_11), .Q(out_12));  // open: Qn, preset, en, reset
  D_Flip_Flop d_ff_4 (.clk(clock_1_out), .D(out_12), .Q(out_13));  // open: Qn, preset, en, reset
  D_Flip_Flop d_ff_5 (.clk(clock_1_out), .D(out_13), .Q(out_14));  // open: Qn, preset, en, reset
  D_Flip_Flop d_ff_6 (.clk(clock_1_out), .D(out_14), .Q(out_15));  // open: Qn, preset, en, reset
  D_Flip_Flop d_ff_7 (.clk(clock_1_out), .D(out_15), .Q(out_16));  // open: Qn, preset, en, reset
  D_Flip_Flop d_ff_8 (.clk(clock_1_out), .D(out_16), .Q(out_17));  // open: Qn, preset, en, reset
endmodule

module main_2 (
  input  in_1,
  input  in_2,
  input  in_3,
  input  in_4,
  input  in_5,
  input  in_6,
  input  in_7,
  input  PI,
  input  in_9,
  input  in_10,
  input  in_11,
  input  in_12,
  input  in_13,
  input  in_14,
  input  in_15,
  input  in_16,
  input  PI_2,
  output out_18,
  output out_19,
  output out_20,
  output out_21,
  output out_22,
  output out_23,
  output out_24,
  output out_25
);

  wire clock_1_out, d_ff_1_q, d_ff_2_q, d_ff_3_q, multiplexer_1_out, multiplexer_2_out, multiplexer_3_out,
       multiplexer_4_out;

  Multiplexer multiplexer_1 (.in0(in_9), .in1(in_10), .out(multiplexer_1_out), .sel(in_1));  // open: en
  D_Flip_Flop d_ff_1 (.clk(clock_1_out), .D(multiplexer_1_out), .Q(d_ff_1_q));  // open: Qn, preset, en, reset
  Multiplexer multiplexer_2 (.in0(d_ff_1_q), .in1(in_11), .out(multiplexer_2_out), .sel(in_2));  // open: en
  D_Flip_Flop d_ff_2 (.clk(clock_1_out), .D(multiplexer_2_out), .Q(d_ff_2_q));  // open: Qn, preset, en, reset
  Multiplexer multiplexer_3 (.in0(d_ff_2_q), .in1(in_12), .out(multiplexer_3_out), .sel(in_3));  // open: en
  D_Flip_Flop d_ff_3 (.clk(clock_1_out), .D(multiplexer_3_out), .Q(d_ff_3_q));  // open: Qn, preset, en, reset
  Multiplexer multiplexer_4 (.in0(d_ff_3_q), .in1(in_13), .out(multiplexer_4_out), .sel(in_4));  // open: en
  D_Flip_Flop d_ff_4 (.clk(clock_1_out), .D(multiplexer_4_out), .Q(out_23));  // open: Qn, preset, en, reset
  D_Flip_Flop d_ff_5 (.clk(clock_1_out));  // open: D, Q, Qn, preset, en, reset
  D_Flip_Flop d_ff_6 (.clk(clock_1_out));  // open: D, Q, Qn, preset, en, reset
  D_Flip_Flop d_ff_7 (.clk(clock_1_out));  // open: D, Q, Qn, preset, en, reset
  D_Flip_Flop d_ff_8 (.clk(clock_1_out));  // open: D, Q, Qn, preset, en, reset
  Clock clock_1 (.out(clock_1_out));
endmodule

module main_3 (
  input  in_1,
  output out_2
);

  Multiplexer multiplexer_1 (.sel(in_1));  // open: in0, in1, out, en
endmodule
