// Logisim project test-left.circ as structural Verilog: 3 circuits, main circuit main
module main (
  input  Left_in,
  input  In,
  output out_3,
  output out_4,
  output out_5,
  output out_6,
  output out_7,
  output out_8,
  output out_9,
  output out_10
);

  wire CLK_out, multiplexer_1_out, multiplexer_2_out, multiplexer_3_out, multiplexer_4_out,
       multiplexer_5_out, multiplexer_6_out, multiplexer_7_out, multiplexer_8_out;

  Clock CLK (.out(CLK_out));
  Multiplexer multiplexer_1 (.in1(In), .out(multiplexer_1_out), .sel(Left_in));  // open: in0, en
  D_Flip_Flop d_ff_1 (.clk(CLK_out), .D(multiplexer_1_out), .Q(out_3));  // open: Qn, preset, en, reset
  Multiplexer multiplexer_2 (.in1(out_3), .out(multiplexer_2_out), .sel(Left_in));  // open: in0, en
  D_Flip_Flop d_ff_2 (.clk(CLK_out), .D(multiplexer_2_out), .Q(out_4));  // open: Qn, preset, en, reset
  Multiplexer multiplexer_3 (.in1(out_4), .out(multiplexer_3_out), .sel(Left_in));  // open: in0, en
  D_Flip_Flop d_ff_3 (.clk(CLK_out), .D(multiplexer_3_out), .Q(out_5));  // open: Qn, preset, en, reset
  Multiplexer multiplexer_4 (.in1(out_5), .out(multiplexer_4_out), .sel(Left_in));  // open: in0, en
  D_Flip_Flop d_ff_4 (.clk(CLK_out), .D(multiplexer_4_out), .Q(out_7));  // open: Qn, preset, en, reset
  Multiplexer multiplexer_5 (.in1(out_7), .out(multiplexer_5_out), .sel(Left_in));  // open: in0, en
  D_Flip_Flop d_ff_5 (.clk(CLK_out), .D(multiplexer_5_out), .Q(out_9));  // open: Qn, preset, en, reset
  Multiplexer multiplexer_6 (.in1(out_9), .out(multiplexer_6_out), .sel(Left_in));  // open: in0, en
  D_Flip_Flop d_ff_6 (.clk(CLK_out), .D(multiplexer_6_out), .Q(out_6));  // open: Qn, preset, en, reset
  Multiplexer multiplexer_7 (.in1(out_6), .out(multiplexer_7_out), .sel(Left_in));  // open: in0, en
  D_Flip_Flop d_ff_7 (.clk(CLK_out), .D(multiplexer_7_out), .Q(out_10));  // open: Qn, preset, en, reset
  Multiplexer multiplexer_8 (.in0(In), .in1(out_10), .out(multiplexer_8_out), .sel(Left_in));  // open: en
  D_Flip_Flop d_ff_8 (.clk(CLK_out), .D(multiplexer_8_out), .Q(out_8));  // open: Qn, preset, en, reset
endmodule

module right (
  input  Left_in,
  input  In,
  output out_3,
  output out_4,
  output out_5,
  output out_6,
  output out_7,
  output out_8,
  output out_9,
  output out_10
);

  wire clock_1_out, multiplexer_1_out, multiplexer_2_out, multiplexer_3_out, multiplexer_4_out,
       multiplexer_5_out, multiplexer_6_out, multiplexer_7_out, multiplexer_8_out;

  Clock clock_1 (.out(clock_1_out));
  D_Flip_Flop d_ff_1 (.clk(clock_1_out), .D(multiplexer_1_out), .Q(out_4));  // open: Qn, preset, en, reset
  Multiplexer multiplexer_1 (.in0(out_3), .out(multiplexer_1_out), .sel(Left_in));  // open: in1, en
  D_Flip_Flop d_ff_2 (.clk(clock_1_out), .D(multiplexer_2_out), .Q(out_3));  // open: Qn, preset, en, reset
  Multiplexer multiplexer_2 (.in0(out_8), .out(multiplexer_2_out), .sel(Left_in));  // open: in1, en
  D_Flip_Flop d_ff_3 (.clk(clock_1_out), .D(multiplexer_3_out), .Q(out_8));  // open: Qn, preset, en, reset
  Multiplexer multiplexer_3 (.in0(out_5), .out(multiplexer_3_out), .sel(Left_in));  // open: in1, en
  Multiplexer multiplexer_4 (.in0(out_6), .out(multiplexer_4_out), .sel(Left_in));  // open: in1, en
  D_Flip_Flop d_ff_4 (.clk(clock_1_out), .D(multiplexer_4_out), .Q(out_5));  // open: Qn, preset, en, reset
  D_Flip_Flop d_ff_5 (.clk(clock_1_out), .D(multiplexer_5_out), .Q(out_6));  // open: Qn, preset, en, reset
  Multiplexer multiplexer_5 (.in0(out_7), .out(multiplexer_5_out), .sel(Left_in));  // open: in1, en
  D_Flip_Flop d_ff_6 (.clk(clock_1_out), .D(multiplexer_6_out), .Q(out_7));  // open: Qn, preset, en, reset
  Multiplexer multiplexer_6 (.in0(out_9), .out(multiplexer_6_out), .sel(Left_in));  // open: in1, en
  Multiplexer multiplexer_7 (.in0(out_10), .out(multiplexer_7_out), .sel(Left_in));  // open: in1, en
  D_Flip_Flop d_ff_7 (.clk(clock_1_out), .D(multiplexer_7_out), .Q(out_9));  // open: Qn, preset, en, reset
  D_Flip_Flop d_ff_8 (.clk(clock_1_out), .D(multiplexer_8_out), .Q(out_10));  // open: Qn, preset, en, reset
  Multiplexer multiplexer_8 (.in0(In), .out(multiplexer_8_out), .sel(Left_in));  // open: in1, en
endmodule

module Combined (
  input  in4,
  input  in5,
  input  in6,
  input  in7,
  input  in0,
  input  in1,
  input  in2,
  input  in3,
  input  left_in,
  input  in4_2,
  input  in5_2,
  input  in6_2,
  input  in7_2,
  input  in0_2,
  input  in1_2,
  input  in2_2,
  input  in3_2,
  output out0,
  output out1,
  output out2,
  output out3,
  output out4,
  output out5,
  output out6,
  output out7
);

  wire CLK_2_out, CLK_out;

  Clock CLK (.out(CLK_out));
  Clock CLK_2 (.out(CLK_2_out));
  D_Flip_Flop d_ff_1 (.clk(CLK_out));  // open: D, Q, Qn, preset, en, reset
  Multiplexer multiplexer_1 (.sel(left_in));  // open: in0, in1, out, en
  D_Flip_Flop d_ff_2 (.clk(CLK_2_out));  // open: D, Q, Qn, preset, en, reset
  Multiplexer multiplexer_2 ();  // open: in0, in1, out, sel, en
  Multiplexer multiplexer_3 ();  // open: in0, in1, out, sel, en
  Multiplexer multiplexer_4 (.sel(left_in));  // open: in0, in1, out, en
  D_Flip_Flop d_ff_3 (.clk(CLK_out));  // open: D, Q, Qn, preset, en, reset
  D_Flip_Flop d_ff_4 (.clk(CLK_2_out));  // open: D, Q, Qn, preset, en, reset
  Multiplexer multiplexer_5 ();  // open: in0, in1, out, sel, en
  Multiplexer multiplexer_6 ();  // open: in0, in1, out, sel, en
  Multiplexer multiplexer_7 (.sel(left_in));  // open: in0, in1, out, en
  D_Flip_Flop d_ff_5 (.clk(CLK_out));  // open: D, Q, Qn, preset, en, reset
  Multiplexer multiplexer_8 (.sel(left_in));  // open: in0, in1, out, en
  D_Flip_Flop d_ff_6 (.clk(CLK_2_out));  // open: D, Q, Qn, preset, en, reset
  Multiplexer multiplexer_9 ();  // open: in0, in1, out, sel, en
  Multiplexer multiplexer_10 ();  // open: in0, in1, out, sel, en
  D_Flip_Flop d_ff_7 (.clk(CLK_out));  // open: D, Q, Qn, preset, en, reset
  Multiplexer multiplexer_11 (.sel(left_in));  // open: in0, in1, out, en
  D_Flip_Flop d_ff_8 (.clk(CLK_2_out));  // open: D, Q, Qn, preset, en, reset
  Multiplexer multiplexer_12 ();  // open: in0, in1, out, sel, en
  Multiplexer multiplexer_13 ();  // open: in0, in1, out, sel, en
  Multiplexer multiplexer_14 (.sel(left_in));  // open: in0, in1, out, en
  D_Flip_Flop d_ff_9 (.clk(CLK_out));  // open: D, Q, Qn, preset, en, reset
  Multiplexer multiplexer_15 ();  // open: in0, in1, out, sel, en
  D_Flip_Flop d_ff_10 (.clk(CLK_2_out));  // open: D, Q, Qn, preset, en, reset
  Multiplexer multiplexer_16 ();  // open: in0, in1, out, sel, en
  Multiplexer multiplexer_17 (.sel(left_in));  // open: in0, in1, out, en
  D_Flip_Flop d_ff_11 (.clk(CLK_out));  // open: D, Q, Qn, preset, en, reset
  Multiplexer multiplexer_18 ();  // open: in0, in1, out, sel, en
  D_Flip_Flop d_ff_12 (.clk(CLK_2_out));  // open: D, Q, Qn, preset, en, reset
  Multiplexer multiplexer_19 ();  // open: in0, in1, out, sel, en
  Multiplexer multiplexer_20 (.sel(left_in));  // open: in0, in1, out, en
  D_Flip_Flop d_ff_13 (.clk(CLK_out));  // open: D, Q, Qn, preset, en, reset
  D_Flip_Flop d_ff_14 (.clk(CLK_2_out));  // open: D, Q, Qn, preset, en, reset
  Multiplexer multiplexer_21 ();  // open: in0, in1, out, sel, en
  Multiplexer multiplexer_22 ();  // open: in0, in1, out, sel, en
  D_Flip_Flop d_ff_15 (.clk(CLK_out));  // open: D, Q, Qn, preset, en, reset
  D_Flip_Flop d_ff_16 (.clk(CLK_2_out));  // open: D, Q, Qn, preset, en, reset
  Multiplexer multiplexer_23 ();  // open: in0, in1, out, sel, en
  Multiplexer multiplexer_24 ();  // open: in0, in1, out, sel, en
endmodule
